// Logisim project CPU.circ as structural Verilog: 4 circuits, main circuit Main
module ALU (
  input  [15:0] A,
  input  [15:0] B,
  input  [3:0] OPCD,
  output [15:0] out_4
);

  wire and_3_out, and_4_out, and_5_out, not_1_out, not_2_out;
  wire [1:0] M;
  wire [15:0] adder_1_out, adder_2_out, divider_1_out, multiplexer_1_out, multiplexer_2_out,
       multiplexer_3_out, multiplier_1_out, negator_1_out, subtractor_1_out, subtractor_2_out;

  not not_1 (not_1_out, OPCD[2]);
  not not_2 (not_2_out, OPCD[3]);
  and and_1 (M[1], OPCD[3], not_1_out);
  and and_2 (M[0], not_2_out, OPCD[2]);
  and and_3 (and_3_out, OPCD[3], OPCD[2]);
  and and_4 (and_4_out, OPCD[0], OPCD[1]);
  and and_5 (and_5_out, and_3_out, and_4_out);
  Adder #(.width(16)) adder_1 (.a(A), .b(B), .out(adder_1_out));  // open: cin, cout
  Subtractor #(.width(16)) subtractor_1 (.a(A), .b(B), .out(subtractor_1_out));  // open: bin, bout
  Multiplier #(.width(16)) multiplier_1 (.a(A), .b(B), .out(multiplier_1_out));  // open: cin, cout
  Divider #(.width(16)) divider_1 (.a(A), .b(B), .out(divider_1_out));  // open: upper, rem
  Adder #(.width(16)) adder_2 (.a(B), .b(16'h1), .out(adder_2_out));  // open: cin, cout
  Subtractor #(.width(16)) subtractor_2 (.a(B), .b(16'h1), .out(subtractor_2_out));  // open: bin, bout
  Negator #(.width(16)) negator_1 (.in(B), .out(negator_1_out));
  Multiplexer #(.select(2), .width(16)) multiplexer_1 (
    .in0(adder_1_out), .in1(subtractor_1_out), .in2(multiplier_1_out), .in3(divider_1_out),
    .out(multiplexer_1_out), .sel(OPCD[1:0]));
  Multiplexer #(.select(2), .width(16)) multiplexer_2 (
    .in0({16{1'b0}}), .in1(adder_2_out), .in2(subtractor_2_out), .in3(negator_1_out),
    .out(multiplexer_2_out), .sel(OPCD[1:0]));
  Multiplexer #(.select(2), .width(16)) multiplexer_3 (
    .in0({16{1'b0}}), .in1(multiplexer_2_out), .in2(multiplexer_1_out), .in3({16{1'b0}}),
    .out(multiplexer_3_out), .sel(M));
  Multiplexer #(.width(16)) multiplexer_4 (.in0(multiplexer_3_out), .in1(B), .out(out_4), .sel(and_5_out));

  // Other names for the same wires on the sheet: C[1:0] = OPCD[1:0]

  // Notes on the sheet:
  //   op entre dois n ?
  //   \/
  //   10 = 2N
  //   01 = 1N
  //   1111 = COPY
  //   DOIS N
  //   UM N
  //   NOT
  //   ADD
  //   SUB
  //   MULT
  //   DIV
  //   STPU
  //   STPD
  //   00: +
  //   01: -
  //   10: X
  //   11: /
endmodule

module Lab (
  input  in_1,
  input  in_2,
  input  in_3,
  input  [4:0] in_4,
  input  [4:0] in_5,
  input  [3:0] in_6
);

  // RGB_Video #(.height(32), .scale(8), .width(32)) rgb_video_1: pin names not known; wires that end beside it: in_1, in_2, in_3, in_4, in_5, in_6
endmodule

module CPU (
  input  CLOCK,
  input  [6:0] UserInput,
  input  [15:0] Instruction,
  output [13:0] ADDRESS,
  output [1:0] DDFF,
  output SAVE,
  output HALT,
  output FETCH,
  output [15:0] regA,
  output [15:0] regB,
  output JUMP,
  output [15:0] regD,
  output [15:0] regC,
  output [4:0] MAP_Y,
  output [4:0] MAP_X,
  output WHITE,
  output SCREEN,
  output BLACK,
  output START,
  output BUFF,
  output [11:0] FREQ,
  output SOUND
);

  wire and_1_out, and_2_out, and_3_out, and_4_out, and_9_out, and_10_out, and_11_out, and_12_out, and_23_out,
       and_24_out, and_25_out, and_26_out, bA, bB, bC, bD, comparator_2_eq, comparator_3_eq, comparator_6_eq,
       comparator_7_eq, comparator_8_eq, comparator_9_eq, comparator_10_eq, comparator_11_eq,
       comparator_12_eq, comparator_13_eq, comparator_14_eq, comparator_15_eq, comparator_16_eq,
       comparator_17_eq, comparator_18_eq, comparator_18_gt, comparator_18_lt, comparator_19_eq,
       comparator_20_eq, comparator_21_eq, comparator_22_eq, eA, eB, eC, eD, mA, MAT, mB, mC, mD, nand_1_out,
       not_1_out, not_2_out, not_3_out, not_4_out, not_5_out, not_6_out, not_7_out, or_1_out, or_2_out,
       or_3_out, or_4_out, or_6_out;
  wire [15:0] alu_1_out_4, multiplexer_1_out, multiplexer_2_out, multiplexer_3_out, multiplexer_4_out,
       multiplexer_5_out, multiplexer_6_out, multiplexer_7_out, multiplexer_8_out, multiplexer_10_out,
       multiplexer_11_out, multiplexer_13_out, multiplexer_14_out, wA, wB, wC, wD, wmA, wmB, wmC, wmD;
  wire [15:2] register_2_q;
  wire [15:5] multiplexer_12_out, multiplexer_15_out;

  Multiplexer #(.width(16)) multiplexer_1 (.in0(wA), .in1(wmA), .out(multiplexer_1_out), .sel(mA));
  or or_1 (or_1_out, eA, mA, bA);
  Multiplexer #(.width(16)) multiplexer_2 (.in0(wC), .in1(wmC), .out(multiplexer_2_out), .sel(mC));
  or or_2 (or_2_out, eC, mC, bC);
  Multiplexer #(.width(16)) multiplexer_3 (
    .in0(multiplexer_1_out), .in1({{9{1'b0}}, UserInput}), .out(multiplexer_3_out), .sel(BUFF));
  Multiplexer #(.width(16)) multiplexer_4 (
    .in0(multiplexer_2_out), .in1({{9{1'b0}}, UserInput}), .out(multiplexer_4_out), .sel(BUFF));
  Comparator #(.width(16)) comparator_1 (.a(Instruction), .b(16'hf0f), .eq(HALT));  // open: gt, lt
  Register #(.width(16)) RA (.D(multiplexer_3_out), .en(or_1_out), .clk(CLOCK), .Q(regA));  // open: clr
  Register #(.width(16)) RC (.D(multiplexer_4_out), .en(or_2_out), .clk(CLOCK), .Q(regC));  // open: clr
  Multiplexer #(.width(16)) multiplexer_5 (.in0(wB), .in1(wmB), .out(multiplexer_5_out), .sel(mB));
  or or_3 (or_3_out, eB, mB, bB);
  Multiplexer #(.width(16)) multiplexer_6 (.in0(wD), .in1(wmD), .out(multiplexer_6_out), .sel(mD));
  or or_4 (or_4_out, eD, mD, bD);
  Demultiplexer #(.select(2), .width(16)) demultiplexer_1 (
    .out0(wA), .out1(wB), .out2(wC), .out3(wD), .in(Instruction), .sel(DDFF));
  Multiplexer #(.width(16)) multiplexer_7 (
    .in0(multiplexer_5_out), .in1({{9{1'b0}}, UserInput}), .out(multiplexer_7_out), .sel(BUFF));
  Multiplexer #(.width(16)) multiplexer_8 (
    .in0(multiplexer_6_out), .in1({{9{1'b0}}, UserInput}), .out(multiplexer_8_out), .sel(BUFF));
  Register #(.width(16)) RB (.D(multiplexer_7_out), .en(or_3_out), .clk(CLOCK), .Q(regB));  // open: clr
  Register #(.width(16)) RD (.D(multiplexer_8_out), .en(or_4_out), .clk(CLOCK), .Q(regD));  // open: clr
  and and_1 (and_1_out, Instruction[14], Instruction[15]);
  Register #(.width(14)) register_1 (.D(Instruction[13:0]), .en(and_1_out), .clk(CLOCK), .Q(ADDRESS));  // open: clr
  Register #(.width(16)) register_2 (.D(Instruction), .en(1'b1), .clk(CLOCK), .Q({register_2_q, DDFF}));  // open: clr
  not not_1 (not_1_out, register_2_q[15]);
  Comparator #(.width(4)) comparator_2 (.a(register_2_q[15:12]), .b(4'b1000), .eq(comparator_2_eq));  // open: gt, lt
  Comparator #(.width(4)) comparator_3 (.a(register_2_q[15:12]), .b(4'b1010), .eq(comparator_3_eq));  // open: gt, lt
  Comparator #(.width(4)) comparator_4 (.a(register_2_q[15:12]), .b(4'b0100), .eq(MAT));  // open: gt, lt
  and and_2 (and_2_out, register_2_q[12], register_2_q[13], register_2_q[14]);
  Multiplexer #(.width(12)) multiplexer_9 (.in0({12{1'b0}}), .in1({register_2_q[11:2], DDFF}), .out(FREQ), .sel(SOUND));
  and and_3 (and_3_out, register_2_q[12], register_2_q[15]);
  not not_2 (not_2_out, register_2_q[13]);
  and and_4 (and_4_out, not_2_out, not_3_out);
  not not_3 (not_3_out, register_2_q[14]);
  Comparator #(.width(4)) comparator_5 (.a(register_2_q[15:12]), .b(4'b1011), .eq(SCREEN));  // open: gt, lt
  and and_5 (BUFF, and_2_out, not_1_out);
  and and_6 (SOUND, and_3_out, and_4_out);
  Comparator #(.width(2)) comparator_6 (.a(DDFF), .b(2'b00), .eq(comparator_6_eq));  // open: gt, lt
  Comparator #(.width(2)) comparator_7 (.a(DDFF), .b(2'b01), .eq(comparator_7_eq));  // open: gt, lt
  Multiplexer #(.select(2), .width(16)) multiplexer_10 (
    .in0(regA), .in1(regB), .in2(regC), .in3(regD), .out(multiplexer_10_out), .sel(register_2_q[5:4]));
  Comparator #(.width(2)) comparator_8 (.a(DDFF), .b(2'b00), .eq(comparator_8_eq));  // open: gt, lt
  Comparator #(.width(2)) comparator_9 (.a(DDFF), .b(2'b01), .eq(comparator_9_eq));  // open: gt, lt
  not not_4 (not_4_out, register_2_q[11]);
  Multiplexer #(.select(2), .width(16)) multiplexer_11 (
    .in0(regA), .in1(regB), .in2(regC), .in3(regD), .out(multiplexer_11_out), .sel(register_2_q[5:4]));
  Multiplexer #(.select(2), .width(16)) multiplexer_12 (
    .in0(regA), .in1(regB), .in2(regC), .in3(regD), .out({multiplexer_12_out, MAP_Y}), .sel(register_2_q[5:4]));
  and and_7 (eA, comparator_6_eq, FETCH);
  and and_8 (eB, comparator_7_eq, FETCH);
  and and_9 (and_9_out, register_2_q[11], comparator_2_eq);
  and and_10 (and_10_out, comparator_2_eq, not_4_out);
  Comparator #(.width(4)) comparator_10 (.a(register_2_q[11:8]), .b(4'b0000), .eq(comparator_10_eq));  // open: gt, lt
  Comparator #(.width(4)) comparator_11 (.a(register_2_q[11:8]), .b(4'b0001), .eq(comparator_11_eq));  // open: gt, lt
  Comparator #(.width(4)) comparator_12 (.a(register_2_q[11:8]), .b(4'b0010), .eq(comparator_12_eq));  // open: gt, lt
  Comparator #(.width(4)) comparator_13 (.a(register_2_q[11:8]), .b(4'b0011), .eq(comparator_13_eq));  // open: gt, lt
  and and_11 (and_11_out, register_2_q[10], register_2_q[11]);
  not not_5 (not_5_out, register_2_q[10]);
  and and_12 (and_12_out, not_5_out, register_2_q[11]);
  and and_13 (bA, comparator_8_eq, BUFF);
  and and_14 (bB, comparator_9_eq, BUFF);
  Multiplexer #(.select(2), .width(16)) multiplexer_13 (
    .in0(regA), .in1(regB), .in2(regC), .in3(regD), .out(multiplexer_13_out), .sel(register_2_q[7:6]));
  nand nand_1 (nand_1_out, register_2_q[10], register_2_q[11]);
  Comparator #(.width(2)) comparator_14 (.a(DDFF), .b(2'b10), .eq(comparator_14_eq));  // open: gt, lt
  Comparator #(.width(2)) comparator_15 (.a(DDFF), .b(2'b11), .eq(comparator_15_eq));  // open: gt, lt
  Multiplexer #(.select(2), .width(16)) multiplexer_14 (
    .in0(regA), .in1(regB), .in2(regC), .in3(regD), .out(multiplexer_14_out), .sel(register_2_q[7:6]));
  Multiplexer #(.select(2), .width(16)) multiplexer_15 (
    .in0(regA), .in1(regB), .in2(regC), .in3(regD), .out({multiplexer_15_out, MAP_X}), .sel(register_2_q[7:6]));
  and and_15 (WHITE, and_11_out, SCREEN);
  and and_16 (BLACK, nand_1_out, SCREEN);
  and and_17 (START, and_12_out, SCREEN);
  Comparator #(.width(2)) comparator_16 (.a(DDFF), .b(2'b10), .eq(comparator_16_eq));  // open: gt, lt
  Comparator #(.width(2)) comparator_17 (.a(DDFF), .b(2'b11), .eq(comparator_17_eq));  // open: gt, lt
  and and_18 (eC, comparator_14_eq, FETCH);
  and and_19 (eD, comparator_15_eq, FETCH);
  and and_20 (SAVE, and_9_out, not_6_out);
  not not_6 (not_6_out, CLOCK);
  or or_5 (FETCH, and_9_out, and_10_out);
  Comparator #(.width(16)) comparator_18 (
    .a(multiplexer_13_out), .b(multiplexer_10_out), .gt(comparator_18_gt), .eq(comparator_18_eq),
    .lt(comparator_18_lt));
  and and_21 (bC, comparator_16_eq, BUFF);
  and and_22 (bD, comparator_17_eq, BUFF);
  and and_23 (and_23_out, comparator_18_gt, comparator_10_eq);
  and and_24 (and_24_out, comparator_18_lt, comparator_11_eq);
  not not_7 (not_7_out, comparator_18_eq);
  and and_25 (and_25_out, not_7_out, comparator_12_eq);
  and and_26 (and_26_out, comparator_18_eq, comparator_13_eq);
  Comparator #(.width(2)) comparator_19 (.a(DDFF), .b(2'b00), .eq(comparator_19_eq));  // open: gt, lt
  Comparator #(.width(2)) comparator_20 (.a(DDFF), .b(2'b01), .eq(comparator_20_eq));  // open: gt, lt
  and and_27 (mA, comparator_19_eq, MAT);
  and and_28 (mB, comparator_20_eq, MAT);
  ALU alu_1 (.A(multiplexer_14_out), .B(multiplexer_11_out), .OPCD(register_2_q[11:8]), .out_4(alu_1_out_4));
  or or_6 (or_6_out, and_23_out, and_24_out, and_25_out, and_26_out);
  Demultiplexer #(.select(2), .width(16)) demultiplexer_2 (
    .out0(wmA), .out1(wmB), .out2(wmC), .out3(wmD), .in(alu_1_out_4), .sel(DDFF));
  and and_29 (JUMP, or_6_out, comparator_3_eq);
  Comparator #(.width(2)) comparator_21 (.a(DDFF), .b(2'b10), .eq(comparator_21_eq));  // open: gt, lt
  Comparator #(.width(2)) comparator_22 (.a(DDFF), .b(2'b11), .eq(comparator_22_eq));  // open: gt, lt
  and and_30 (mC, comparator_21_eq, MAT);
  and and_31 (mD, comparator_22_eq, MAT);

  // Other names for the same wires on the sheet: CLK = CLOCK; dA[15:0] = regA; dB[15:0] = regB; dC[15:0] = regC;
  //   dD[15:0] = regD; UsInput[6:0] = UserInput

  // Notes on the sheet:
  //   #00
  //   #10
  //   Valor ASCII
  //   PARSING DAS INSTRUCOES
  //   #01
  //   #11
  //   Se 11 em H3
  //   //Sinal de endereço
  //   Guarda a instruçao anterior
  //   SAVE
  //   LOAD
  //   BUFFER
  //   R
  //   E
  //   G
  //   S
  //   H2
  //   H3
  //   r2
  //   r1
  //   ar
  //   gs
  //   r2
  //   r1
  //   ARG
  //   de
  //   st
  //   arg
  //   DEST/FONTE
  //   H2 = ARGS
  //   H1 = REGS
  //   DEST
  //   /\
  //   Começam com 100 em H3
  //   H3 == 1010 => Instruçao de JUMP
  //   0 == LOAD | 1 == SAVE
  //   ARGS
  //   0 = JGT; 1 = JLT
  //   2 = JNQ; 3 = JEQ;
  //   JUMP?
  //   ARITMETICA = 0100 EM H3
  //   R2
  //   R2
  //   SAVE
  //   LOAD
  //   START
  //   LOAD (DEST)
  //   R2
  //   WHITE
  //   BLACK
  //   LOAD == FETCH
  //   R1
  //   R1
  //   R1
  //   BUFF (DEST)
  //   ARGS
  //   0000 = PAINT BLACK
  //   1100 = PAINT WHITE
  //   1000 = START SCREEN (PAINT ALL BLACK)
endmodule

module Main (
  input  SoundEnable,
  input  Reset,
  input  Reset_2,
  output [15:0] out_4,
  output [15:0] out_5,
  output [13:0] out_6,
  output [15:0] out_7,
  output [13:0] out_8,
  output [15:0] out_9,
  output [15:0] out_10,
  output [6:0] out_11
);

  wire and_1_out, and_2_out, and_3_out, BLACK, BUFF, CLK, clock_2_out, FETCH, HALT, JUMP, keyboard_1_avail,
       not_1_out, not_2_out, SAVE, SCREEN, SOUND, START, WHITE;
  wire [1:0] DDFF;
  wire [3:0] rgb_video_1_p6;
  wire [4:0] MAP_X, MAP_Y;
  wire [11:0] FREQ;
  wire [13:0] multiplexer_1_out;
  wire [15:0] ram_1_dout;

  LED led_1 (.in(FETCH));
  LED led_2 (.in(HALT));
  and and_1 (and_1_out, FETCH, SoundEnable);
  // Buzzer buzzer_1: pin names not known; wires that end beside it: 14'h1ff, and_1_out, 7'b1110000
  not not_1 (not_1_out, FETCH);
  and and_2 (and_2_out, CLK, not_2_out);
  not not_2 (not_2_out, HALT);
  Counter #(.max('h3fff), .width(14)) counter_1 (
    .clr(Reset), .load(JUMP), .up(1'b1), .count(not_1_out), .clk(and_2_out), .D(out_6), .Q(out_8));  // open: carry
  LED led_3 (.in(BUFF));
  // Buzzer buzzer_2: pin names not known; wires that end beside it: {2'b00, FREQ}, SOUND, 7'b1110000
  and and_3 (and_3_out, BUFF, SoundEnable);
  // Buzzer buzzer_3: pin names not known; wires that end beside it: 14'h300, and_3_out, 7'b1110000
  Multiplexer #(.width(14)) multiplexer_1 (.in0(out_8), .in1(out_6), .out(multiplexer_1_out), .sel(FETCH));
  Pull_Resistor pull_resistor_1 (.node(FETCH));
  // RGB_Video #(.height(32), .scale(8), .width(32)) rgb_video_1: pin names not known; wires that end beside it: START, CLK, SCREEN, MAP_X, MAP_Y, rgb_video_1_p6
  LED led_4 (.in(WHITE));
  LED led_5 (.in(BLACK));
  Multiplexer #(.select(2), .width(16)) multiplexer_2 (
    .in0(out_4), .in1(out_5), .in2(out_7), .in3(out_9), .out(out_10), .sel(DDFF));
  Multiplexer #(.width(4)) multiplexer_3 (.in0(4'b0000), .in1(4'b1111), .out(rgb_video_1_p6), .sel(WHITE));
  Clock clock_1 (.out(CLK));
  Pull_Resistor pull_resistor_2 (.node(multiplexer_1_out));
  RAM #(.addrWidth(14), .dataWidth(16), .trigger("high")) ram_1 (
    .addr(multiplexer_1_out), .we(SAVE), .oe(1'b1), .din(out_10), .dout(ram_1_dout));
  Clock clock_2 (.out(clock_2_out));
  Keyboard #(.buflen(16)) keyboard_1 (
    .clk(clock_2_out), .re(BUFF), .clr(Reset_2), .avail(keyboard_1_avail), .data(out_11));
  Pull_Resistor pull_resistor_3 (.node(keyboard_1_avail));
  CPU cpu_1 (
    .CLOCK(CLK), .UserInput(out_11), .Instruction(ram_1_dout), .ADDRESS(out_6), .DDFF(DDFF), .SAVE(SAVE),
    .HALT(HALT), .FETCH(FETCH), .regA(out_4), .regB(out_5), .JUMP(JUMP), .regD(out_9), .regC(out_7),
    .MAP_Y(MAP_Y), .MAP_X(MAP_X), .WHITE(WHITE), .SCREEN(SCREEN), .BLACK(BLACK), .START(START), .BUFF(BUFF),
    .FREQ(FREQ), .SOUND(SOUND));

  // Other names for the same wires on the sheet: ADDRESS[13:0] = out_6; R0[15:0] = out_4; R1[15:0] = out_5;
  //   R2[15:0] = out_7; R3[15:0] = out_9

  // Notes on the sheet:
  //   Codigos de endereço começam com 11 em H3
  //   Cada endereço tem 14 bits
  //   Reset
  //   X
  //   Y
  //   HIGH TRIGGER => OUTPUT SAI NA HORA
  //   Mas tambem escreve na hora...
  //   Keyboard Buffer
endmodule
